# Fritzing sketch FSR (saved by Fritzing 0.9.0b)
circuit board: 8.46667cm x 5.64444cm
breadboards: 1

parts:
  Spark_Core = Spark Core (v1.0)
  FSR = Basic Force Sensing Resistor (FSR) [package=THT]
  Rm = Resistor [tolerance=±5% resistance=220k package=THT]
  U1 = LM 358 Dual Op-Amp [package="DIP8 [THT]"]  # not connected

nets:
  N1: Spark_Core.A0, FSR.pin_1, Rm.Pin_1
  N2: Spark_Core.GND, Rm.Pin_0
  N3: Spark_Core.3V3*, FSR.pin_0
