# Fritzing sketch SparkFSR (saved by Fritzing 0.9.0b)
circuit board: 8.46667cm x 5.64444cm
breadboards: 1

parts:
  FSR = Basic Force Sensing Resistor (FSR) [package=THT]
  Part1 = Spark Core (v1.0)

nets:
  N1: FSR.pin_0, Part1.A6
  N2: FSR.pin_1, Part1.3V3*, Part1.3V3

notes:
  Enable pull-down resistor in Spark code.
